// Logisim project ALU.circ as structural Verilog
module ALU_SHIFTER (
  input  [31:0] B__32,
  input  [4:0] Sa__5,
  input  [3:0] Op__4,
  output [31:0] C__32
);

  wire bitselector_1_out, bitselector_2_out;

  BitSelector #(.width(4)) bitselector_1 (.in(Op__4), .out(bitselector_1_out), .sel(2'b00));
  BitSelector #(.width(4)) bitselector_2 (.in(Op__4), .out(bitselector_2_out), .sel(2'b10));
  _32_BIT_SHIFTER u_32_bit_shifter_1 (
    .Input__1(B__32), .Sa__5(Sa__5), .Cin(bitselector_1_out), .Direction__1(bitselector_2_out), .out_5(C__32));
endmodule

module ALU (
  input  [31:0] A__32,
  input  [31:0] B__32,
  input  [4:0] Sa__5,
  input  [3:0] Op__4,
  output [31:0] Output,
  output Overflow
);

  wire bitselector_1_out, bitselector_2_out, bitselector_3_out, bitselector_4_out;
  wire [31:0] alu_shifter_1_c__32, and_1_out, eq32_1_output, gt32_1_output, lt32_1_output, main_1_out_4,
       ne32_1_output, nor_1_out, or_1_out, xor_1_out;

  BitSelector #(.width(4)) bitselector_1 (.in(Op__4), .out(bitselector_1_out), .sel(2'b00));
  BitSelector #(.width(4)) bitselector_2 (.in(Op__4), .out(bitselector_2_out), .sel(2'b01));
  BitSelector #(.width(4)) bitselector_3 (.in(Op__4), .out(bitselector_3_out), .sel(2'b10));
  BitSelector #(.width(4)) bitselector_4 (.in(Op__4), .out(bitselector_4_out), .sel(2'b11));
  assign and_1_out = B__32 & A__32;  // AND_Gate and_1, 32 bits wide
  assign or_1_out = A__32 | B__32;  // OR_Gate or_1, 32 bits wide
  eq32 eq32_1 (.A(A__32), .B(B__32), .Output(eq32_1_output));
  ne32 ne32_1 (.A(A__32), .B(B__32), .Output(ne32_1_output));
  gt32 gt32_1 (.A(A__32), .B(B__32), .Output(gt32_1_output));
  lt32 lt32_1 (.A(A__32), .B(B__32), .Output(lt32_1_output));
  ALU_SHIFTER alu_shifter_1 (.B__32(B__32), .Sa__5(Sa__5), .Op__4(Op__4), .C__32(alu_shifter_1_c__32));
  assign xor_1_out = A__32 ^ B__32;  // XOR_Gate xor_1, 32 bits wide
  assign nor_1_out = ~(A__32 | B__32);  // NOR_Gate nor_1, 32 bits wide
  AddSubtract32_main main_1 (
    .A(A__32), .in_2(B__32), .AddSubtractChange(bitselector_3_out), .out_4(main_1_out_4), .Overflow(Overflow));
  Multiplexer #(.select(4), .width(32), .enable("false")) multiplexer_1 (
    .in0(alu_shifter_1_c__32), .in1(alu_shifter_1_c__32), .in2(main_1_out_4), .in3(main_1_out_4),
    .in4(alu_shifter_1_c__32), .in5(alu_shifter_1_c__32), .in6(main_1_out_4), .in7(main_1_out_4),
    .in8(and_1_out), .in9(eq32_1_output), .in10(or_1_out), .in11(ne32_1_output), .in12(xor_1_out),
    .in13(gt32_1_output), .in14(nor_1_out), .in15(lt32_1_output), .out(Output), .sel(Op__4));
endmodule

module Correct_ALU (
  input  [31:0] A__32,
  input  [31:0] B__32,
  input  [4:0] Sa__5,
  input  [3:0] Op__4,
  output [31:0] Output,
  output Overflow
);

  wire bitselector_1_out, bitselector_2_out, bitselector_3_out, bitselector_4_out;
  wire [31:0] alu_shifter_1_c__32, and_1_out, eq32_1_output, gt32_1_output, lt32_1_output, main_1_out_4,
       ne32_1_output, nor_1_out, or_1_out, xor_1_out;

  BitSelector #(.width(4)) bitselector_1 (.in(Op__4), .out(bitselector_1_out), .sel(2'b00));
  BitSelector #(.width(4)) bitselector_2 (.in(Op__4), .out(bitselector_2_out), .sel(2'b01));
  BitSelector #(.width(4)) bitselector_3 (.in(Op__4), .out(bitselector_3_out), .sel(2'b10));
  BitSelector #(.width(4)) bitselector_4 (.in(Op__4), .out(bitselector_4_out), .sel(2'b11));
  assign and_1_out = B__32 & A__32;  // AND_Gate and_1, 32 bits wide
  assign or_1_out = A__32 | B__32;  // OR_Gate or_1, 32 bits wide
  eq32 eq32_1 (.A(A__32), .B(B__32), .Output(eq32_1_output));
  ne32 ne32_1 (.A(A__32), .B(B__32), .Output(ne32_1_output));
  gt32 gt32_1 (.A(A__32), .B(B__32), .Output(gt32_1_output));
  lt32 lt32_1 (.A(A__32), .B(B__32), .Output(lt32_1_output));
  ALU_SHIFTER alu_shifter_1 (.B__32(B__32), .Sa__5(Sa__5), .Op__4(Op__4), .C__32(alu_shifter_1_c__32));
  assign xor_1_out = A__32 ^ B__32;  // XOR_Gate xor_1, 32 bits wide
  assign nor_1_out = ~(A__32 | B__32);  // NOR_Gate nor_1, 32 bits wide
  AddSubtract32_main main_1 (
    .A(A__32), .in_2(B__32), .AddSubtractChange(bitselector_3_out), .out_4(main_1_out_4), .Overflow(Overflow));
  Multiplexer #(.select(4), .width(32), .enable("false")) multiplexer_1 (
    .in0(alu_shifter_1_c__32), .in1(alu_shifter_1_c__32), .in2(main_1_out_4), .in3(main_1_out_4),
    .in4(alu_shifter_1_c__32), .in5(alu_shifter_1_c__32), .in6(main_1_out_4), .in7(main_1_out_4),
    .in8(and_1_out), .in9(eq32_1_output), .in10(or_1_out), .in11(ne32_1_output), .in12(xor_1_out),
    .in13(gt32_1_output), .in14(nor_1_out), .in15(lt32_1_output), .out(Output), .sel(Op__4));
endmodule
