// Logisim project Add32.circ as structural Verilog: 5 circuits, main circuit main
module main (
  input  [31:0] A,
  input  [31:0] B,
  input  in_3,
  output [31:0] Out,
  output Overflow,
  output Carry_out
);

  wire sixteen_bit_adder_1_carry_out, sixteen_bit_adder_1_overflow, sixteen_bit_adder_2_overflow;

  Sixteen_Bit_Adder sixteen_bit_adder_1 (
    .in_1(A[15:0]), .in_2(B[15:0]), .C_in(in_3), .out_4(Out[15:0]), .Overflow(sixteen_bit_adder_1_overflow),
    .Carry_out(sixteen_bit_adder_1_carry_out));
  Sixteen_Bit_Adder sixteen_bit_adder_2 (
    .in_1(A[31:16]), .in_2(B[31:16]), .C_in(sixteen_bit_adder_1_carry_out), .out_4(Out[31:16]),
    .Overflow(sixteen_bit_adder_2_overflow), .Carry_out(Carry_out));
  xor xor_1 (Overflow, sixteen_bit_adder_1_overflow, sixteen_bit_adder_2_overflow);

  // Notes on the sheet:
  //   Carry in
endmodule

module One_Bit_Adder (
  input  A,
  input  B,
  input  C_in,
  output S,
  output C_out
);

  wire and_1_out, and_2_out, xor_1_out;

  xor xor_1 (xor_1_out, A, B);
  xor xor_2 (S, xor_1_out, C_in);
  and and_1 (and_1_out, xor_1_out, C_in);
  and and_2 (and_2_out, A, B);
  or or_1 (C_out, and_1_out, and_2_out);
endmodule

module Four_Bit_Adder (
  input  [3:0] A__4,
  input  [3:0] B__4,
  input  C_in,
  output [3:0] Out,
  output Carry_out,
  output Overflow
);

  wire one_bit_adder_1_c_out, one_bit_adder_2_c_out, one_bit_adder_3_c_out;

  One_Bit_Adder one_bit_adder_1 (.A(A__4[0]), .B(B__4[0]), .C_in(C_in), .S(Out[0]), .C_out(one_bit_adder_1_c_out));
  One_Bit_Adder one_bit_adder_2 (
    .A(A__4[1]), .B(B__4[1]), .C_in(one_bit_adder_1_c_out), .S(Out[1]), .C_out(one_bit_adder_2_c_out));
  One_Bit_Adder one_bit_adder_3 (
    .A(A__4[2]), .B(B__4[2]), .C_in(one_bit_adder_2_c_out), .S(Out[2]), .C_out(one_bit_adder_3_c_out));
  One_Bit_Adder one_bit_adder_4 (.A(A__4[3]), .B(B__4[3]), .C_in(one_bit_adder_3_c_out), .S(Out[3]), .C_out(Carry_out));
  xor xor_1 (Overflow, Carry_out, one_bit_adder_3_c_out);
endmodule

module Eight_Bit_Adder (
  input  [7:0] in_1,
  input  C_in,
  input  [7:0] in_3,
  output [7:0] Out,
  output Carry_out,
  output Overflow
);

  wire four_bit_adder_1_carry_out, four_bit_adder_1_overflow, four_bit_adder_2_overflow;

  Four_Bit_Adder four_bit_adder_1 (
    .A__4(in_1[3:0]), .B__4(in_3[3:0]), .C_in(C_in), .Out(Out[3:0]), .Carry_out(four_bit_adder_1_carry_out),
    .Overflow(four_bit_adder_1_overflow));
  Four_Bit_Adder four_bit_adder_2 (
    .A__4(in_1[7:4]), .B__4(in_3[7:4]), .C_in(four_bit_adder_1_carry_out), .Out(Out[7:4]),
    .Carry_out(Carry_out), .Overflow(four_bit_adder_2_overflow));
  xor xor_1 (Overflow, four_bit_adder_2_overflow, four_bit_adder_1_overflow);

  // Notes on the sheet:
  //   A (8)
  //   B (8)
endmodule

module Sixteen_Bit_Adder (
  input  [15:0] in_1,
  input  [15:0] in_2,
  input  C_in,
  output [15:0] out_4,
  output Overflow,
  output Carry_out
);

  wire eight_bit_adder_1_carry_out, eight_bit_adder_1_overflow, eight_bit_adder_2_overflow;

  Eight_Bit_Adder eight_bit_adder_1 (
    .in_1(in_1[7:0]), .C_in(C_in), .in_3(in_2[7:0]), .Out(out_4[7:0]),
    .Carry_out(eight_bit_adder_1_carry_out), .Overflow(eight_bit_adder_1_overflow));
  Eight_Bit_Adder eight_bit_adder_2 (
    .in_1(in_1[15:8]), .C_in(eight_bit_adder_1_carry_out), .in_3(in_2[15:8]), .Out(out_4[15:8]),
    .Carry_out(Carry_out), .Overflow(eight_bit_adder_2_overflow));
  xor xor_1 (Overflow, eight_bit_adder_1_overflow, eight_bit_adder_2_overflow);

  // Notes on the sheet:
  //   A in (16)
  //   B in (16)
  //   Out (16)
endmodule
