// Logisim project AddSubtract32.circ as structural Verilog: 1 circuit, main circuit main
module main (
  input  [31:0] A,
  input  [31:0] in_2,
  input  AddSubtractChange,
  output [31:0] out_4,
  output Overflow
);

  wire [31:0] multiplexer_1_out, not_1_out;

  Multiplexer #(.width(32), .enable("false")) multiplexer_1 (
    .in0(in_2), .in1(not_1_out), .out(multiplexer_1_out), .sel(AddSubtractChange));
  assign not_1_out = ~in_2;  // NOT_Gate not_1, 32 bits wide
  Add32_main main_1 (.A(A), .B(multiplexer_1_out), .Out(out_4), .in_3(AddSubtractChange), .Overflow(Overflow));

  // Notes on the sheet:
  //   B
  //   0 = Add
  //   1 = Subtract
  //   Out (32)
endmodule
