// Logisim project CONTROL MODULE.circ as structural Verilog: 5 circuits, main circuit FunctDeterm_R_Type
module FunctDeterm_R_Type (
  input  [5:0] in_1,
  output [3:0] out_2
);

  Multiplexer #(.select(5), .width(4), .enable("false")) multiplexer_1 (
    .in0(4'b0000), .in1(4'b0000), .in2(4'b0100), .in3(4'b0101), .in4(4'b0000), .in5(4'b0000), .in6(4'b0000),
    .in7(4'b0000), .in8(4'b0000), .in9(4'b0000), .in10(4'b0000), .in11(4'b0000), .in12(4'b0000),
    .in13(4'b0000), .in14(4'b0000), .in15(4'b0000), .in16(4'b0010), .in17(4'b0010), .in18(4'b0110),
    .in19(4'b0110), .in20(4'b1000), .in21(4'b1010), .in22(4'b1100), .in23(4'b1110), .in24(4'b0000),
    .in25(4'b0000), .in26(4'b1111), .in27(4'b1111), .in28(4'b0000), .in29(4'b0000), .in30(4'b0000),
    .in31(4'b0000), .out(out_2), .sel({in_1[5], in_1[3:0]}));
endmodule

module I_Type (
  input  [31:0] Input_32,
  output [15:0] immediate,
  output [4:0] dest,
  output [4:0] src,
  output [3:0] opcode
);

  FunctDeterm_I_Type functdeterm_i_type_1 (.Input(Input_32[31:26]), .out_2(opcode));

  assign dest = Input_32[20:16];
  assign immediate = Input_32[15:0];
  assign src = Input_32[25:21];
endmodule

module R_Type (
  input  [31:0] Input_32,
  output [3:0] Opcode,
  output [4:0] Shift,
  output [4:0] dest,
  output [4:0] src2,
  output [4:0] src1
);

  FunctDeterm_R_Type functdeterm_r_type_1 (.in_1(Input_32[5:0]), .out_2(Opcode));

  assign dest = Input_32[15:11];
  assign Shift = Input_32[10:6];
  assign src1 = Input_32[25:21];
  assign src2 = Input_32[20:16];
endmodule

module FunctDeterm_I_Type (
  input  [5:0] Input,
  output [3:0] out_2
);

  Multiplexer #(.select(3), .width(4), .enable("false")) multiplexer_1 (
    .in0(4'b0000), .in1(4'b0010), .in2(4'b1111), .in3(4'b1111), .in4(4'b1000), .in5(4'b1010), .in6(4'b1100),
    .in7(4'b0000), .out(out_2), .sel(Input[2:0]));
endmodule

module Control (
  input  [31:0] Input_32,
  output [4:0] RD,
  output [4:0] RT,
  output [3:0] OpCode,
  output [4:0] shift,
  output [4:0] dest,
  output [4:0] src2,
  output [4:0] src1,
  output [15:0] immediate
);

  wire bitselector_1_out, not_1_out;
  wire [31:0] transistor_1_out, transistor_2_out;

  BitSelector #(.width(32)) bitselector_1 (.in(Input_32), .out(bitselector_1_out), .sel(5'b11101));
  Transistor #(.\type ("n"), .width(32)) transistor_1 (.in(Input_32), .out(transistor_1_out), .gate(not_1_out));
  not not_1 (not_1_out, bitselector_1_out);
  Transistor #(.\type ("n"), .width(32)) transistor_2 (.in(Input_32), .out(transistor_2_out), .gate(bitselector_1_out));
  R_Type r_type_1 (.Input_32(transistor_1_out), .Opcode(OpCode), .Shift(shift), .dest(dest), .src2(src2), .src1(src1));
  I_Type i_type_1 (.Input_32(transistor_2_out), .immediate(immediate), .dest(dest), .src(src1), .opcode(OpCode));

  assign RD = Input_32[15:11];
  assign RT = Input_32[20:16];
endmodule
