// Logisim project CPU Project.circ as structural Verilog
module ALU_SHIFTER (
  input  [31:0] B__32,
  input  [4:0] Sa__5,
  input  [3:0] Op__4,
  output [31:0] C__32
);

  wire bitselector_1_out, bitselector_2_out;

  BitSelector #(.width(4)) bitselector_1 (.in(Op__4), .out(bitselector_1_out), .sel(2'b00));
  BitSelector #(.width(4)) bitselector_2 (.in(Op__4), .out(bitselector_2_out), .sel(2'b10));
  _32_BIT_SHIFTER u_32_bit_shifter_1 (
    .Input__32(B__32), .Sa__5(Sa__5), .Cin(bitselector_1_out), .Direction__1(bitselector_2_out), .out_5(C__32));
endmodule

module ALU (
  input  [31:0] A__32,
  input  [31:0] B__32,
  input  [4:0] Sa__5,
  input  [3:0] Op__4
);

  wire and_2_out, bitselector_1_out, bitselector_2_out, bitselector_3_out, bitselector_4_out, not_2_out;
  wire [31:0] alu_shifter_1_c__32, and_1_out, multiplexer_1_out, not_3_out, or_1_out, transistor_1_out,
       transistor_2_out, transistor_3_out, transistor_4_out, xor_1_out;

  assign xor_1_out = B__32 ^ A__32;  // XOR_Gate xor_1, 32 bits wide
  assign and_1_out = A__32 & B__32;  // AND_Gate and_1, 32 bits wide
  assign or_1_out = B__32 | A__32;  // OR_Gate or_1, 32 bits wide
  Transistor #(.\type ("n"), .gate("br"), .width(32)) transistor_1 (
    .in(B__32), .out(transistor_1_out), .gate(bitselector_1_out));
  // NOT_Gate not_1 has open pins: in=bitselector_1_out, out=open
  BitSelector #(.width(4)) bitselector_1 (.in(Op__4), .out(bitselector_1_out), .sel(2'b11));
  BitSelector #(.width(4)) bitselector_2 (.in(Op__4), .out(bitselector_2_out), .sel(2'b10));
  not not_2 (not_2_out, bitselector_4_out);
  BitSelector #(.width(4)) bitselector_3 (.in(Op__4), .out(bitselector_3_out), .sel(2'b01));
  BitSelector #(.width(4)) bitselector_4 (.in(Op__4), .out(bitselector_4_out), .sel(2'b00));
  Transistor #(.\type ("n"), .gate("br"), .width(32)) transistor_2 (
    .in(xor_1_out), .out(transistor_2_out), .gate(and_2_out));
  Transistor #(.\type ("n"), .gate("br"), .width(32)) transistor_3 (
    .in(and_1_out), .out(transistor_3_out), .gate(and_2_out));
  Transistor #(.\type ("n"), .gate("br"), .width(32)) transistor_4 (
    .in(B__32), .out(transistor_4_out), .gate(bitselector_2_out));
  Transistor #(.\type ("n"), .gate("br"), .width(32)) transistor_5 (.in(or_1_out), .out(B__32), .gate(and_2_out));
  and and_2 (and_2_out, bitselector_1_out, not_2_out);
  assign not_3_out = ~transistor_4_out;  // NOT_Gate not_3, 32 bits wide
  Multiplexer #(.width(32), .enable("false")) multiplexer_1 (
    .in1(alu_shifter_1_c__32), .out(multiplexer_1_out), .sel(bitselector_3_out));  // open: in0
  ALU_SHIFTER alu_shifter_1 (.B__32(transistor_1_out), .Sa__5(Sa__5), .Op__4(Op__4), .C__32(alu_shifter_1_c__32));
endmodule
