// Logisim project CPU.circ as structural Verilog: 1 circuit, main circuit CPU
module CPU (
  output [31:0] Result
);

  wire clock_1_out, Decode_i_type, ID_EX_i_type_2, MEM_WB_load_store_2, Memory_p11, not_1_out, not_2_out,
       not_3_out, not_4_out, not_5_out;
  wire [3:0] Decode_opcode, Execute_opcode_2, ID_EX_opcode_2;
  wire [4:0] Decode_rd, Decode_rt, Decode_shift, Execute_rd_2, Execute_rt_2, Fetch_clock_2,
       ID_EX_clock_data_2, ID_EX_rd_2, ID_EX_rt_2, ID_EX_shift_2, IF_ID_clock_data_2;
  wire [15:0] Decode_immediate, ID_EX_immediate_2;
  wire [31:0] Decode_a, Decode_b, EX_MEM_b_2, EX_MEM_d_2, Execute_a_2, Execute_b_2, Execute_d,
       Execute_target, Fetch_instructions, ID_EX_a_2, ID_EX_b_2, IF_ID_instructions_data_2, MEM_WB_d_2,
       MEM_WB_m_2, Memory_p9, Memory_p10;

  Clock clock_1 (.out(clock_1_out));
  Fetch Fetch (.Clock(not_1_out), .Instructions(Fetch_instructions), .Clock_2(Fetch_clock_2));
  not not_1 (not_1_out, clock_1_out);
  Decode Decode (
    .D(MEM_WB_d_2), .Instruction(IF_ID_instructions_data_2), .Clock(not_2_out), .OpCode(Decode_opcode),
    .Shift(Decode_shift), .A(Decode_a), .B(Decode_b), .Immediate(Decode_immediate), .RT(Decode_rt),
    .RD(Decode_rd), .I_Type(Decode_i_type));
  IF_ID IF_ID (
    .Instructions_Data(Fetch_instructions), .Clock_Data(Fetch_clock_2), .Clock(clock_1_out),
    .Instructions_Data_2(IF_ID_instructions_data_2), .Clock_Data_2(IF_ID_clock_data_2));
  not not_2 (not_2_out, clock_1_out);
  ID_EX ID_EX (
    .OpCode(Decode_opcode), .Shift(Decode_shift), .A(Decode_a), .B(Decode_b), .Immediate(Decode_immediate),
    .RT(Decode_rt), .RD(Decode_rd), .Clock_Data(IF_ID_clock_data_2), .I_Type(Decode_i_type),
    .Clock(clock_1_out), .OpCode_2(ID_EX_opcode_2), .Shift_2(ID_EX_shift_2), .A_2(ID_EX_a_2),
    .B_2(ID_EX_b_2), .Immediate_2(ID_EX_immediate_2), .RT_2(ID_EX_rt_2), .RD_2(ID_EX_rd_2),
    .Clock_Data_2(ID_EX_clock_data_2), .I_Type_2(ID_EX_i_type_2));
  Execute Execute (
    .OpCode(ID_EX_opcode_2), .Shift(ID_EX_shift_2), .A(ID_EX_a_2), .B(ID_EX_b_2),
    .Immediate(ID_EX_immediate_2), .RT(ID_EX_rt_2), .RD(ID_EX_rd_2), .Clock_Data(ID_EX_clock_data_2),
    .Clock(not_3_out), .UI(ID_EX_i_type_2), .A_2(Execute_a_2), .D(Execute_d), .B_2(Execute_b_2),
    .Target(Execute_target), .OpCode_2(Execute_opcode_2), .RT_2(Execute_rt_2), .RD_2(Execute_rd_2));
  not not_3 (not_3_out, clock_1_out);
  EX_MEM EX_MEM (
    .A(Execute_a_2), .D(Execute_d), .B(Execute_b_2), .Target(Execute_target), .OpCode(Execute_opcode_2),
    .RT(Execute_rt_2), .RD(Execute_rd_2), .Clock(clock_1_out), .D_2(EX_MEM_d_2), .B_2(EX_MEM_b_2));  // open: A_2, Target_2, OpCode_2, RT_2, RD_2
  not not_4 (not_4_out, clock_1_out);
  // MEMORY_MODULE_main Memory: pin names not known; wires that end beside it: Execute_b_2, Execute_target, Execute_opcode_2, Execute_rt_2, Execute_rd_2, EX_MEM_d_2, EX_MEM_b_2, not_4_out, Memory_p9, Memory_p10, Memory_p11
  MEM_WB_main MEM_WB (
    .D(Memory_p9), .M(Memory_p10), .Load_Store(Memory_p11), .Clock(clock_1_out), .D_2(MEM_WB_d_2),
    .M_2(MEM_WB_m_2), .Load_Store_2(MEM_WB_load_store_2));  // open: OpCode, RT, RD, OpCode_2, RT_2, RD_2
  not not_5 (not_5_out, clock_1_out);
  WRITEBACK_MODULE_main Writeback (
    .D(MEM_WB_d_2), .Loadd_Store(MEM_WB_load_store_2), .M(MEM_WB_m_2), .Clock(not_5_out), .result(Result));
endmodule
