// Logisim project Comparator32.circ as structural Verilog: 4 circuits, main circuit eq32
module eq32 (
  input  [31:0] A,
  input  [31:0] B,
  output [31:0] Output
);

  wire [31:0] and_1_out, and_2_out, nor_1_out, not_1_out, not_2_out;

  assign not_1_out = ~A;  // NOT_Gate not_1, 32 bits wide
  assign not_2_out = ~B;  // NOT_Gate not_2, 32 bits wide
  assign and_1_out = not_1_out & B;  // AND_Gate and_1, 32 bits wide
  assign and_2_out = A & not_2_out;  // AND_Gate and_2, 32 bits wide
  assign nor_1_out = ~(and_1_out | and_2_out);  // NOR_Gate nor_1, 32 bits wide
  and and_3 (Output[0], nor_1_out[0], nor_1_out[1], nor_1_out[2], nor_1_out[3], nor_1_out[4], nor_1_out[5], nor_1_out[6], nor_1_out[7], nor_1_out[8], nor_1_out[9], nor_1_out[10], nor_1_out[11], nor_1_out[12], nor_1_out[13], nor_1_out[14], nor_1_out[15], nor_1_out[16], nor_1_out[17], nor_1_out[18], nor_1_out[19], nor_1_out[20], nor_1_out[21], nor_1_out[22], nor_1_out[23], nor_1_out[24], nor_1_out[25], nor_1_out[26], nor_1_out[27], nor_1_out[28], nor_1_out[29], nor_1_out[30], nor_1_out[31]);

  assign Output[31:1] = {31{1'b0}};
endmodule

module ne32 (
  input  [31:0] A,
  input  [31:0] B,
  output [31:0] Output
);

  wire and_3_out;
  wire [31:0] and_1_out, and_2_out, nor_1_out, not_1_out, not_2_out;

  assign not_1_out = ~A;  // NOT_Gate not_1, 32 bits wide
  assign not_2_out = ~B;  // NOT_Gate not_2, 32 bits wide
  assign and_1_out = not_1_out & B;  // AND_Gate and_1, 32 bits wide
  assign and_2_out = A & not_2_out;  // AND_Gate and_2, 32 bits wide
  assign nor_1_out = ~(and_1_out | and_2_out);  // NOR_Gate nor_1, 32 bits wide
  not not_3 (Output[0], and_3_out);
  and and_3 (and_3_out, nor_1_out[0], nor_1_out[1], nor_1_out[2], nor_1_out[3], nor_1_out[4], nor_1_out[5], nor_1_out[6], nor_1_out[7], nor_1_out[8], nor_1_out[9], nor_1_out[10], nor_1_out[11], nor_1_out[12], nor_1_out[13], nor_1_out[14], nor_1_out[15], nor_1_out[16], nor_1_out[17], nor_1_out[18], nor_1_out[19], nor_1_out[20], nor_1_out[21], nor_1_out[22], nor_1_out[23], nor_1_out[24], nor_1_out[25], nor_1_out[26], nor_1_out[27], nor_1_out[28], nor_1_out[29], nor_1_out[30], nor_1_out[31]);

  assign Output[31:1] = {31{1'b0}};
endmodule

module lt32 (
  input  [31:0] A,
  input  [31:0] B,
  output [31:0] Output
);

  wire and_1_out, bitselector_1_out, not_1_out;
  wire [31:0] main_1_out_4;

  AddSubtract32_main main_1 (.A(A), .in_2(B), .AddSubtractChange(1'b1), .out_4(main_1_out_4));  // open: Overflow
  BitSelector #(.width(32)) bitselector_1 (.in(main_1_out_4), .out(bitselector_1_out), .sel({5{1'b1}}));
  not not_1 (not_1_out, bitselector_1_out);
  and and_1 (and_1_out, not_1_out, 1'b1);
  not not_2 (Output[0], and_1_out);

  assign Output[31:1] = {31{1'b0}};
endmodule

module gt32 (
  input  [31:0] A,
  input  [31:0] B,
  output [31:0] Output
);

  wire bitselector_1_out, bitselector_2_out, not_1_out;
  wire [31:0] eq32_1_output, main_1_out_4, not_2_out;

  AddSubtract32_main main_1 (.A(A), .in_2(B), .AddSubtractChange(1'b1), .out_4(main_1_out_4));  // open: Overflow
  not not_1 (not_1_out, bitselector_1_out);
  BitSelector #(.width(32)) bitselector_1 (.in(main_1_out_4), .out(bitselector_1_out), .sel({5{1'b1}}));
  eq32 eq32_1 (.A(B), .B(A), .Output(eq32_1_output));
  assign not_2_out = ~eq32_1_output;  // NOT_Gate not_2, 32 bits wide
  BitSelector #(.width(32)) bitselector_2 (.in(not_2_out), .out(bitselector_2_out), .sel({5{1'b0}}));
  and and_1 (Output[0], not_1_out, 1'b1, bitselector_2_out);

  assign Output[31:1] = {31{1'b0}};
endmodule
