// Logisim project Control32.circ as structural Verilog
module main (
  input  [31:0] in_1,
  output W,
  output [4:0] Rw,
  output [4:0] Ra,
  output [4:0] Rb,
  output [3:0] Op
);
endmodule

module FunctionDeterm (
  input  in_1,
  input  in_2,
  input  in_3,
  input  in_4,
  input  in_5,
  input  in_6,
  output [3:0] out_7
);

  Multiplexer #(.select(5), .width(4), .enable("false")) multiplexer_1 (
    .in0(4'b0000), .in1(4'b0000), .in2(4'b0100), .in3(4'b0101), .in4(4'b0000), .in5(4'b0000), .in6(4'b0000),
    .in7(4'b0000), .in8(4'b0000), .in9(4'b0000), .in10(4'b0000), .in11(4'b0000), .in12(4'b0000),
    .in13(4'b0000), .in14(4'b0000), .in15(4'b0000), .in16(4'b0010), .in17(4'b0010), .in18(4'b0110),
    .in19(4'b0110), .in20(4'b1000), .in21(4'b1010), .in22(4'b1100), .in23(4'b1110), .in24(4'b0000),
    .in25(4'b0000), .in26(4'b1111), .in27(4'b1111), .in28(4'b0000), .in29(4'b0000), .in30(4'b0000),
    .in31(4'b0000), .out(out_7), .sel({in_6, in_4, in_3, in_2, in_1}));
endmodule
