// Logisim project Control[3258].circ as structural Verilog
module Control (
  input  [31:0] Instr,
  input  in_2,
  output [3:0] Op,
  output W,
  output [4:0] Rw,
  output [4:0] Ra,
  output [4:0] Rb
);

  wire I_out, not_1_out, transistor_1_out;

  and I (I_out, Instr[29], not_1_out);
  not not_1 (not_1_out, Instr[31]);
  Transistor #(.\type ("n")) transistor_1 (.in(in_2), .out(transistor_1_out), .gate(I_out));
endmodule

module funct (
  input  in_1,
  input  in_2,
  input  in_3,
  input  in_4,
  input  in_5,
  input  in_6,
  output [3:0] out_7
);

  Multiplexer #(.select(5), .width(4), .enable("false")) multiplexer_1 (
    .in0(4'b0000), .in1(4'b0000), .in2(4'b0100), .in3(4'b0101), .in4(4'b0000), .in5(4'b0000), .in6(4'b0000),
    .in7(4'b0000), .in8(4'b0000), .in9(4'b0000), .in10(4'b0000), .in11(4'b0000), .in12(4'b0000),
    .in13(4'b0000), .in14(4'b0000), .in15(4'b0000), .in16(4'b0010), .in17(4'b0010), .in18(4'b0110),
    .in19(4'b0110), .in20(4'b1000), .in21(4'b1010), .in22(4'b1100), .in23(4'b1110), .in24(4'b0000),
    .in25(4'b0000), .in26(4'b1111), .in27(4'b1111), .in28(4'b0000), .in29(4'b0000), .in30(4'b0000),
    .in31(4'b0000), .out(out_7), .sel({in_6, in_4, in_3, in_2, in_1}));
endmodule
