// Logisim project DECODE MODULE.circ as structural Verilog: 1 circuit, main circuit Decode
module Decode (
  input  [31:0] D,
  input  [31:0] Instruction,
  input  Clock,
  output [3:0] OpCode,
  output [4:0] Shift,
  output [31:0] A,
  output [31:0] B,
  output [15:0] Immediate,
  output [4:0] RT,
  output [4:0] RD,
  output I_Type
);

  wire [4:0] control_1_dest, control_1_src1, control_1_src2;

  Control control_1 (
    .Input_32(Instruction), .RD(RD), .RT(RT), .OpCode(OpCode), .shift(Shift), .dest(control_1_dest),
    .src2(control_1_src2), .src1(control_1_src1), .immediate(Immediate), .I_Type(I_Type));
  Register32 register32_1 (
    .in_1(D), .W(1'b1), .Rw(control_1_dest), .Ra(control_1_src1), .Rb(control_1_src2), .Clk(Clock),
    .out_7(A), .out_8(B));
endmodule
