// Logisim project EXECUTE MODULE.circ as structural Verilog: 1 circuit, main circuit Execute
module Execute (
  input  [3:0] OpCode,
  input  [4:0] Shift,
  input  [31:0] A,
  input  [31:0] B,
  input  UI,
  input  [15:0] Immediate,
  input  [4:0] RT,
  input  [4:0] RD,
  input  [4:0] Clock_Data,
  input  Clock,
  output [31:0] A_2,
  output [31:0] D,
  output [31:0] B_2,
  output [31:0] Target,
  output [3:0] OpCode_2,
  output [4:0] RT_2,
  output [4:0] RD_2
);

  wire [31:0] bit_extender_1_out, bit_extender_2_out, multiplexer_1_out;

  assign bit_extender_1_out = {{16{1'b0}}, Immediate};  // Bit_Extender bit_extender_1
  Multiplexer #(.width(32), .enable("false")) multiplexer_1 (
    .in0(B), .in1(bit_extender_1_out), .out(multiplexer_1_out), .sel(UI));
  Adder #(.width(32)) adder_1 (.a(bit_extender_1_out), .b(bit_extender_2_out), .out(Target));  // open: cin, cout
  assign bit_extender_2_out = {{27{1'b0}}, Clock_Data};  // Bit_Extender bit_extender_2
  Correct_ALU correct_alu_1 (
    .A__32(A), .B__32(multiplexer_1_out), .Sa__5(Shift), .Op__4(OpCode), .Output(D));  // open: Overflow

  assign A_2 = A;
  assign B_2 = B;
  assign OpCode_2 = OpCode;
  assign RD_2 = RD;
  assign RT_2 = RT;
endmodule
