// Logisim project EX_MEM.circ as structural Verilog: 1 circuit, main circuit EX/MEM
module EX_MEM (
  input  [31:0] A,
  input  [31:0] D,
  input  [31:0] B,
  input  [31:0] Target,
  input  [3:0] OpCode,
  input  [4:0] RT,
  input  [4:0] RD,
  input  Clock,
  output [31:0] A_2,
  output [31:0] D_2,
  output [31:0] B_2,
  output [31:0] Target_2,
  output [3:0] OpCode_2,
  output [4:0] RT_2,
  output [4:0] RD_2
);

  Register #(.width(32)) register_1 (.D(A), .Q(A_2), .clk(Clock));  // open: en, clr
  Register #(.width(32)) register_2 (.D(D), .Q(D_2), .clk(Clock));  // open: en, clr
  Register #(.width(32)) register_3 (.D(B), .Q(B_2), .clk(Clock));  // open: en, clr
  Register #(.width(32)) register_4 (.D(Target), .Q(Target_2), .clk(Clock));  // open: en, clr
  Register #(.width(4)) register_5 (.D(OpCode), .Q(OpCode_2), .clk(Clock));  // open: en, clr
  Register #(.width(5)) register_6 (.D(RT), .Q(RT_2), .clk(Clock));  // open: en, clr
  Register #(.width(5)) register_7 (.D(RD), .Q(RD_2), .clk(Clock));  // open: en, clr
endmodule
