// Logisim project FETCH MODULE.circ as structural Verilog: 2 circuits, main circuit Fetch
module Fetch (
  input  Clock,
  output [31:0] Instructions,
  output [4:0] Clock_2
);

  Clock clock_1 (.Clock(Clock), .out_2(Clock_2));
  ROM #(.addrWidth(5), .dataWidth(32)) rom_1 (.addr(Clock_2), .data(Instructions));  // open: sel

  // Notes on the sheet:
  //   contents of rom_1 (hex, n*v repeats v):
  //   25490001 31490001 35490001 29490001 39490001 2d490001 14b4821 14b4823 14b4824 14b4825 14b4826
  //   14b4827 14b482a 14b482b 14b480b 14b480a a4840 a4842 a4843 16a4804 16a4806 16a4807 3c090001
endmodule

module Clock (
  input  Clock,
  output [4:0] out_2
);

  wire [4:0] adder_1_out;

  Adder #(.width(5)) adder_1 (.a(out_2), .b(5'b00001), .out(adder_1_out));  // open: cin, cout
  Register #(.width(5)) register_1 (.D(adder_1_out), .Q(out_2), .clk(Clock));  // open: en, clr
endmodule
