// Logisim project ID_EX.circ as structural Verilog: 1 circuit, main circuit ID/EX
module ID_EX (
  input  [3:0] OpCode,
  input  [4:0] Shift,
  input  [31:0] A,
  input  [31:0] B,
  input  [15:0] Immediate,
  input  [4:0] RT,
  input  [4:0] RD,
  input  [4:0] Clock_Data,
  input  I_Type,
  input  Clock,
  output [3:0] OpCode_2,
  output [4:0] Shift_2,
  output [31:0] A_2,
  output [31:0] B_2,
  output [15:0] Immediate_2,
  output [4:0] RT_2,
  output [4:0] RD_2,
  output [4:0] Clock_Data_2,
  output I_Type_2
);

  Register #(.width(4)) register_1 (.D(OpCode), .Q(OpCode_2), .clk(Clock));  // open: en, clr
  Register #(.width(5)) register_2 (.D(Shift), .Q(Shift_2), .clk(Clock));  // open: en, clr
  Register #(.width(32)) register_3 (.D(A), .Q(A_2), .clk(Clock));  // open: en, clr
  Register #(.width(32)) register_4 (.D(B), .Q(B_2), .clk(Clock));  // open: en, clr
  Register #(.width(16)) register_5 (.D(Immediate), .Q(Immediate_2), .clk(Clock));  // open: en, clr
  Register #(.width(5)) register_6 (.D(RT), .Q(RT_2), .clk(Clock));  // open: en, clr
  Register #(.width(5)) register_7 (.D(RD), .Q(RD_2), .clk(Clock));  // open: en, clr
  Register #(.width(5)) register_8 (.D(Clock_Data), .Q(Clock_Data_2), .clk(Clock));  // open: en, clr
  Register #(.width(1)) register_9 (.D(I_Type), .Q(I_Type_2), .clk(Clock));  // open: en, clr
endmodule
