// Logisim project IF_ID.circ as structural Verilog: 1 circuit, main circuit IF/ID
module IF_ID (
  input  [31:0] Instructions_Data,
  input  [4:0] Clock_Data,
  input  Clock,
  output [31:0] Instructions_Data_2,
  output [4:0] Clock_Data_2
);

  wire not_1_out;

  not not_1 (not_1_out, Clock);
  Register #(.width(32)) register_1 (.D(Instructions_Data), .Q(Instructions_Data_2), .clk(not_1_out));  // open: en, clr
  Register #(.width(5)) register_2 (.D(Clock_Data), .Q(Clock_Data_2), .clk(not_1_out));  // open: en, clr
endmodule
