// Logisim project MEMORY MODULE.circ as structural Verilog: 1 circuit, main circuit main
module main (
  input  [31:0] D,
  input  [31:0] B,
  input  Clk,
  input  Store,
  input  [3:0] OpCode,
  output [31:0] D_2,
  output [31:0] M,
  output Load_Store
);

  RAM #(.addrWidth(16), .dataWidth(32), .bus("separate")) ram_1 (
    .addr(D[15:0]), .din(B), .data(M), .str(Store), .clk(Clk));  // open: sel, ld, clr

  assign D_2 = D;
  assign Load_Store = 1'b0;
endmodule
