// Logisim project MEM_WB.circ as structural Verilog: 1 circuit, main circuit main
module main (
  input  [31:0] D,
  input  [31:0] M,
  input  Load_Store,
  input  [3:0] OpCode,
  input  [4:0] RT,
  input  [4:0] RD,
  input  Clock,
  output [31:0] D_2,
  output [31:0] M_2,
  output Load_Store_2,
  output [3:0] OpCode_2,
  output [4:0] RT_2,
  output [4:0] RD_2
);

  Register #(.width(32)) register_1 (.D(D), .Q(D_2), .clk(Clock));  // open: en, clr
  Register #(.width(32)) register_2 (.D(M), .Q(M_2), .clk(Clock));  // open: en, clr
  Register #(.width(1)) register_3 (.D(Load_Store), .Q(Load_Store_2), .clk(Clock));  // open: en, clr
  Register #(.width(4)) register_4 (.D(OpCode), .Q(OpCode_2), .clk(Clock));  // open: en, clr
  Register #(.width(5)) register_5 (.D(RT), .Q(RT_2), .clk(Clock));  // open: en, clr
  Register #(.width(5)) register_6 (.D(RD), .Q(RD_2), .clk(Clock));  // open: en, clr
endmodule
