// Logisim project Rom32.circ as structural Verilog: 1 circuit, main circuit main
module main (
  input  [4:0] in_1,
  input  in_2,
  output [31:0] out_3
);

  ROM #(.addrWidth(5), .dataWidth(32)) rom_1 (.addr(in_1), .data(out_3), .sel(in_2));

  // Notes on the sheet:
  //   contents of rom_1 (hex, n*v repeats v):
  //   14b4820 11111111 addf ddf ada23232 0 ff 0 322332 0 3e2df3 4*0 2332 0 23e23e23
endmodule
