// Logisim project Shift32.circ as structural Verilog
module _1_BIT_LEFT_SHIFTER (
  input  C_in__1,
  input  [31:0] in_2,
  output [31:0] out_3
);


  assign out_3 = {in_2[30:0], C_in__1};
endmodule

// Left
module _32_BIT_LEFT_SHIFTER (
  input  Cin__1,
  input  [31:0] in_2,
  input  [4:0] SA__5,
  output [31:0] out_4
);

  wire [31:0] n1_bit_left_shifter_1_out_3, n1_bit_left_shifter_2_out_3, n1_bit_left_shifter_3_out_3,
       n1_bit_left_shifter_4_out_3, n1_bit_left_shifter_5_out_3, n1_bit_left_shifter_6_out_3,
       n1_bit_left_shifter_7_out_3, n1_bit_left_shifter_8_out_3, n1_bit_left_shifter_9_out_3,
       n1_bit_left_shifter_10_out_3, n1_bit_left_shifter_11_out_3, n1_bit_left_shifter_12_out_3,
       n1_bit_left_shifter_13_out_3, n1_bit_left_shifter_14_out_3, n1_bit_left_shifter_15_out_3,
       n1_bit_left_shifter_16_out_3, n1_bit_left_shifter_17_out_3, n1_bit_left_shifter_18_out_3,
       n1_bit_left_shifter_19_out_3, n1_bit_left_shifter_20_out_3, n1_bit_left_shifter_21_out_3,
       n1_bit_left_shifter_22_out_3, n1_bit_left_shifter_23_out_3, n1_bit_left_shifter_24_out_3,
       n1_bit_left_shifter_25_out_3, n1_bit_left_shifter_26_out_3, n1_bit_left_shifter_27_out_3,
       n1_bit_left_shifter_28_out_3, n1_bit_left_shifter_29_out_3, n1_bit_left_shifter_30_out_3,
       n1_bit_left_shifter_31_out_3;

  _1_BIT_LEFT_SHIFTER u_1_bit_left_shifter_1 (.C_in__1(Cin__1), .in_2(in_2), .out_3(n1_bit_left_shifter_1_out_3));
  _1_BIT_LEFT_SHIFTER u_1_bit_left_shifter_2 (
    .C_in__1(Cin__1), .in_2(n1_bit_left_shifter_1_out_3), .out_3(n1_bit_left_shifter_2_out_3));
  _1_BIT_LEFT_SHIFTER u_1_bit_left_shifter_3 (
    .C_in__1(Cin__1), .in_2(n1_bit_left_shifter_2_out_3), .out_3(n1_bit_left_shifter_3_out_3));
  _1_BIT_LEFT_SHIFTER u_1_bit_left_shifter_4 (
    .C_in__1(Cin__1), .in_2(n1_bit_left_shifter_3_out_3), .out_3(n1_bit_left_shifter_4_out_3));
  _1_BIT_LEFT_SHIFTER u_1_bit_left_shifter_5 (
    .C_in__1(Cin__1), .in_2(n1_bit_left_shifter_4_out_3), .out_3(n1_bit_left_shifter_5_out_3));
  _1_BIT_LEFT_SHIFTER u_1_bit_left_shifter_6 (
    .C_in__1(Cin__1), .in_2(n1_bit_left_shifter_5_out_3), .out_3(n1_bit_left_shifter_6_out_3));
  _1_BIT_LEFT_SHIFTER u_1_bit_left_shifter_7 (
    .C_in__1(Cin__1), .in_2(n1_bit_left_shifter_6_out_3), .out_3(n1_bit_left_shifter_7_out_3));
  _1_BIT_LEFT_SHIFTER u_1_bit_left_shifter_8 (
    .C_in__1(Cin__1), .in_2(n1_bit_left_shifter_7_out_3), .out_3(n1_bit_left_shifter_8_out_3));
  _1_BIT_LEFT_SHIFTER u_1_bit_left_shifter_9 (
    .C_in__1(Cin__1), .in_2(n1_bit_left_shifter_8_out_3), .out_3(n1_bit_left_shifter_9_out_3));
  _1_BIT_LEFT_SHIFTER u_1_bit_left_shifter_10 (
    .C_in__1(Cin__1), .in_2(n1_bit_left_shifter_9_out_3), .out_3(n1_bit_left_shifter_10_out_3));
  _1_BIT_LEFT_SHIFTER u_1_bit_left_shifter_11 (
    .C_in__1(Cin__1), .in_2(n1_bit_left_shifter_10_out_3), .out_3(n1_bit_left_shifter_11_out_3));
  _1_BIT_LEFT_SHIFTER u_1_bit_left_shifter_12 (
    .C_in__1(Cin__1), .in_2(n1_bit_left_shifter_11_out_3), .out_3(n1_bit_left_shifter_12_out_3));
  _1_BIT_LEFT_SHIFTER u_1_bit_left_shifter_13 (
    .C_in__1(Cin__1), .in_2(n1_bit_left_shifter_12_out_3), .out_3(n1_bit_left_shifter_13_out_3));
  _1_BIT_LEFT_SHIFTER u_1_bit_left_shifter_14 (
    .C_in__1(Cin__1), .in_2(n1_bit_left_shifter_13_out_3), .out_3(n1_bit_left_shifter_14_out_3));
  _1_BIT_LEFT_SHIFTER u_1_bit_left_shifter_15 (
    .C_in__1(Cin__1), .in_2(n1_bit_left_shifter_14_out_3), .out_3(n1_bit_left_shifter_15_out_3));
  _1_BIT_LEFT_SHIFTER u_1_bit_left_shifter_16 (
    .C_in__1(Cin__1), .in_2(n1_bit_left_shifter_15_out_3), .out_3(n1_bit_left_shifter_16_out_3));
  _1_BIT_LEFT_SHIFTER u_1_bit_left_shifter_17 (
    .C_in__1(Cin__1), .in_2(n1_bit_left_shifter_16_out_3), .out_3(n1_bit_left_shifter_17_out_3));
  _1_BIT_LEFT_SHIFTER u_1_bit_left_shifter_18 (
    .C_in__1(Cin__1), .in_2(n1_bit_left_shifter_17_out_3), .out_3(n1_bit_left_shifter_18_out_3));
  _1_BIT_LEFT_SHIFTER u_1_bit_left_shifter_19 (
    .C_in__1(Cin__1), .in_2(n1_bit_left_shifter_18_out_3), .out_3(n1_bit_left_shifter_19_out_3));
  _1_BIT_LEFT_SHIFTER u_1_bit_left_shifter_20 (
    .C_in__1(Cin__1), .in_2(n1_bit_left_shifter_19_out_3), .out_3(n1_bit_left_shifter_20_out_3));
  _1_BIT_LEFT_SHIFTER u_1_bit_left_shifter_21 (
    .C_in__1(Cin__1), .in_2(n1_bit_left_shifter_20_out_3), .out_3(n1_bit_left_shifter_21_out_3));
  _1_BIT_LEFT_SHIFTER u_1_bit_left_shifter_22 (
    .C_in__1(Cin__1), .in_2(n1_bit_left_shifter_21_out_3), .out_3(n1_bit_left_shifter_22_out_3));
  _1_BIT_LEFT_SHIFTER u_1_bit_left_shifter_23 (
    .C_in__1(Cin__1), .in_2(n1_bit_left_shifter_22_out_3), .out_3(n1_bit_left_shifter_23_out_3));
  _1_BIT_LEFT_SHIFTER u_1_bit_left_shifter_24 (
    .C_in__1(Cin__1), .in_2(n1_bit_left_shifter_23_out_3), .out_3(n1_bit_left_shifter_24_out_3));
  _1_BIT_LEFT_SHIFTER u_1_bit_left_shifter_25 (
    .C_in__1(Cin__1), .in_2(n1_bit_left_shifter_24_out_3), .out_3(n1_bit_left_shifter_25_out_3));
  _1_BIT_LEFT_SHIFTER u_1_bit_left_shifter_26 (
    .C_in__1(Cin__1), .in_2(n1_bit_left_shifter_25_out_3), .out_3(n1_bit_left_shifter_26_out_3));
  _1_BIT_LEFT_SHIFTER u_1_bit_left_shifter_27 (
    .C_in__1(Cin__1), .in_2(n1_bit_left_shifter_26_out_3), .out_3(n1_bit_left_shifter_27_out_3));
  _1_BIT_LEFT_SHIFTER u_1_bit_left_shifter_28 (
    .C_in__1(Cin__1), .in_2(n1_bit_left_shifter_27_out_3), .out_3(n1_bit_left_shifter_28_out_3));
  _1_BIT_LEFT_SHIFTER u_1_bit_left_shifter_29 (
    .C_in__1(Cin__1), .in_2(n1_bit_left_shifter_28_out_3), .out_3(n1_bit_left_shifter_29_out_3));
  _1_BIT_LEFT_SHIFTER u_1_bit_left_shifter_30 (
    .C_in__1(Cin__1), .in_2(n1_bit_left_shifter_29_out_3), .out_3(n1_bit_left_shifter_30_out_3));
  _1_BIT_LEFT_SHIFTER u_1_bit_left_shifter_31 (
    .C_in__1(Cin__1), .in_2(n1_bit_left_shifter_30_out_3), .out_3(n1_bit_left_shifter_31_out_3));
  Multiplexer #(.select(5), .width(32), .enable("false")) multiplexer_1 (
    .in0(in_2), .in1(n1_bit_left_shifter_1_out_3), .in2(n1_bit_left_shifter_2_out_3),
    .in3(n1_bit_left_shifter_3_out_3), .in4(n1_bit_left_shifter_4_out_3), .in5(n1_bit_left_shifter_5_out_3),
    .in6(n1_bit_left_shifter_6_out_3), .in7(n1_bit_left_shifter_7_out_3), .in8(n1_bit_left_shifter_8_out_3),
    .in9(n1_bit_left_shifter_9_out_3), .in10(n1_bit_left_shifter_10_out_3),
    .in11(n1_bit_left_shifter_11_out_3), .in12(n1_bit_left_shifter_12_out_3),
    .in13(n1_bit_left_shifter_13_out_3), .in14(n1_bit_left_shifter_14_out_3),
    .in15(n1_bit_left_shifter_15_out_3), .in16(n1_bit_left_shifter_16_out_3),
    .in17(n1_bit_left_shifter_17_out_3), .in18(n1_bit_left_shifter_18_out_3),
    .in19(n1_bit_left_shifter_19_out_3), .in20(n1_bit_left_shifter_20_out_3),
    .in21(n1_bit_left_shifter_21_out_3), .in22(n1_bit_left_shifter_22_out_3),
    .in23(n1_bit_left_shifter_23_out_3), .in24(n1_bit_left_shifter_24_out_3),
    .in25(n1_bit_left_shifter_25_out_3), .in26(n1_bit_left_shifter_26_out_3),
    .in27(n1_bit_left_shifter_27_out_3), .in28(n1_bit_left_shifter_28_out_3),
    .in29(n1_bit_left_shifter_29_out_3), .in30(n1_bit_left_shifter_30_out_3),
    .in31(n1_bit_left_shifter_31_out_3), .out(out_4), .sel(SA__5));
endmodule

// Right
module _32_BIT_RIGHT_SHIFTER (
  input  Cin__1,
  input  [31:0] in_2,
  input  [4:0] SA__5,
  output [31:0] out_4
);

  wire [31:0] n1_bit_right_shifter_1_out_3, n1_bit_right_shifter_2_out_3, n1_bit_right_shifter_3_out_3,
       n1_bit_right_shifter_4_out_3, n1_bit_right_shifter_5_out_3, n1_bit_right_shifter_6_out_3,
       n1_bit_right_shifter_7_out_3, n1_bit_right_shifter_8_out_3, n1_bit_right_shifter_9_out_3,
       n1_bit_right_shifter_10_out_3, n1_bit_right_shifter_11_out_3, n1_bit_right_shifter_12_out_3,
       n1_bit_right_shifter_13_out_3, n1_bit_right_shifter_14_out_3, n1_bit_right_shifter_15_out_3,
       n1_bit_right_shifter_16_out_3, n1_bit_right_shifter_17_out_3, n1_bit_right_shifter_18_out_3,
       n1_bit_right_shifter_19_out_3, n1_bit_right_shifter_20_out_3, n1_bit_right_shifter_21_out_3,
       n1_bit_right_shifter_22_out_3, n1_bit_right_shifter_23_out_3, n1_bit_right_shifter_24_out_3,
       n1_bit_right_shifter_25_out_3, n1_bit_right_shifter_26_out_3, n1_bit_right_shifter_27_out_3,
       n1_bit_right_shifter_28_out_3, n1_bit_right_shifter_29_out_3, n1_bit_right_shifter_30_out_3,
       n1_bit_right_shifter_31_out_3;

  _1_BIT_RIGHT_SHIFTER u_1_bit_right_shifter_1 (.C_in__1(Cin__1), .in_2(in_2), .out_3(n1_bit_right_shifter_1_out_3));
  _1_BIT_RIGHT_SHIFTER u_1_bit_right_shifter_2 (
    .C_in__1(Cin__1), .in_2(n1_bit_right_shifter_1_out_3), .out_3(n1_bit_right_shifter_2_out_3));
  _1_BIT_RIGHT_SHIFTER u_1_bit_right_shifter_3 (
    .C_in__1(Cin__1), .in_2(n1_bit_right_shifter_2_out_3), .out_3(n1_bit_right_shifter_3_out_3));
  _1_BIT_RIGHT_SHIFTER u_1_bit_right_shifter_4 (
    .C_in__1(Cin__1), .in_2(n1_bit_right_shifter_3_out_3), .out_3(n1_bit_right_shifter_4_out_3));
  _1_BIT_RIGHT_SHIFTER u_1_bit_right_shifter_5 (
    .C_in__1(Cin__1), .in_2(n1_bit_right_shifter_4_out_3), .out_3(n1_bit_right_shifter_5_out_3));
  _1_BIT_RIGHT_SHIFTER u_1_bit_right_shifter_6 (
    .C_in__1(Cin__1), .in_2(n1_bit_right_shifter_5_out_3), .out_3(n1_bit_right_shifter_6_out_3));
  _1_BIT_RIGHT_SHIFTER u_1_bit_right_shifter_7 (
    .C_in__1(Cin__1), .in_2(n1_bit_right_shifter_6_out_3), .out_3(n1_bit_right_shifter_7_out_3));
  _1_BIT_RIGHT_SHIFTER u_1_bit_right_shifter_8 (
    .C_in__1(Cin__1), .in_2(n1_bit_right_shifter_7_out_3), .out_3(n1_bit_right_shifter_8_out_3));
  _1_BIT_RIGHT_SHIFTER u_1_bit_right_shifter_9 (
    .C_in__1(Cin__1), .in_2(n1_bit_right_shifter_8_out_3), .out_3(n1_bit_right_shifter_9_out_3));
  _1_BIT_RIGHT_SHIFTER u_1_bit_right_shifter_10 (
    .C_in__1(Cin__1), .in_2(n1_bit_right_shifter_9_out_3), .out_3(n1_bit_right_shifter_10_out_3));
  _1_BIT_RIGHT_SHIFTER u_1_bit_right_shifter_11 (
    .C_in__1(Cin__1), .in_2(n1_bit_right_shifter_10_out_3), .out_3(n1_bit_right_shifter_11_out_3));
  _1_BIT_RIGHT_SHIFTER u_1_bit_right_shifter_12 (
    .C_in__1(Cin__1), .in_2(n1_bit_right_shifter_11_out_3), .out_3(n1_bit_right_shifter_12_out_3));
  _1_BIT_RIGHT_SHIFTER u_1_bit_right_shifter_13 (
    .C_in__1(Cin__1), .in_2(n1_bit_right_shifter_12_out_3), .out_3(n1_bit_right_shifter_13_out_3));
  _1_BIT_RIGHT_SHIFTER u_1_bit_right_shifter_14 (
    .C_in__1(Cin__1), .in_2(n1_bit_right_shifter_13_out_3), .out_3(n1_bit_right_shifter_14_out_3));
  _1_BIT_RIGHT_SHIFTER u_1_bit_right_shifter_15 (
    .C_in__1(Cin__1), .in_2(n1_bit_right_shifter_14_out_3), .out_3(n1_bit_right_shifter_15_out_3));
  _1_BIT_RIGHT_SHIFTER u_1_bit_right_shifter_16 (
    .C_in__1(Cin__1), .in_2(n1_bit_right_shifter_15_out_3), .out_3(n1_bit_right_shifter_16_out_3));
  _1_BIT_RIGHT_SHIFTER u_1_bit_right_shifter_17 (
    .C_in__1(Cin__1), .in_2(n1_bit_right_shifter_16_out_3), .out_3(n1_bit_right_shifter_17_out_3));
  _1_BIT_RIGHT_SHIFTER u_1_bit_right_shifter_18 (
    .C_in__1(Cin__1), .in_2(n1_bit_right_shifter_17_out_3), .out_3(n1_bit_right_shifter_18_out_3));
  _1_BIT_RIGHT_SHIFTER u_1_bit_right_shifter_19 (
    .C_in__1(Cin__1), .in_2(n1_bit_right_shifter_18_out_3), .out_3(n1_bit_right_shifter_19_out_3));
  _1_BIT_RIGHT_SHIFTER u_1_bit_right_shifter_20 (
    .C_in__1(Cin__1), .in_2(n1_bit_right_shifter_19_out_3), .out_3(n1_bit_right_shifter_20_out_3));
  _1_BIT_RIGHT_SHIFTER u_1_bit_right_shifter_21 (
    .C_in__1(Cin__1), .in_2(n1_bit_right_shifter_20_out_3), .out_3(n1_bit_right_shifter_21_out_3));
  _1_BIT_RIGHT_SHIFTER u_1_bit_right_shifter_22 (
    .C_in__1(Cin__1), .in_2(n1_bit_right_shifter_21_out_3), .out_3(n1_bit_right_shifter_22_out_3));
  _1_BIT_RIGHT_SHIFTER u_1_bit_right_shifter_23 (
    .C_in__1(Cin__1), .in_2(n1_bit_right_shifter_22_out_3), .out_3(n1_bit_right_shifter_23_out_3));
  _1_BIT_RIGHT_SHIFTER u_1_bit_right_shifter_24 (
    .C_in__1(Cin__1), .in_2(n1_bit_right_shifter_23_out_3), .out_3(n1_bit_right_shifter_24_out_3));
  _1_BIT_RIGHT_SHIFTER u_1_bit_right_shifter_25 (
    .C_in__1(Cin__1), .in_2(n1_bit_right_shifter_24_out_3), .out_3(n1_bit_right_shifter_25_out_3));
  _1_BIT_RIGHT_SHIFTER u_1_bit_right_shifter_26 (
    .C_in__1(Cin__1), .in_2(n1_bit_right_shifter_25_out_3), .out_3(n1_bit_right_shifter_26_out_3));
  _1_BIT_RIGHT_SHIFTER u_1_bit_right_shifter_27 (
    .C_in__1(Cin__1), .in_2(n1_bit_right_shifter_26_out_3), .out_3(n1_bit_right_shifter_27_out_3));
  _1_BIT_RIGHT_SHIFTER u_1_bit_right_shifter_28 (
    .C_in__1(Cin__1), .in_2(n1_bit_right_shifter_27_out_3), .out_3(n1_bit_right_shifter_28_out_3));
  _1_BIT_RIGHT_SHIFTER u_1_bit_right_shifter_29 (
    .C_in__1(Cin__1), .in_2(n1_bit_right_shifter_28_out_3), .out_3(n1_bit_right_shifter_29_out_3));
  _1_BIT_RIGHT_SHIFTER u_1_bit_right_shifter_30 (
    .C_in__1(Cin__1), .in_2(n1_bit_right_shifter_29_out_3), .out_3(n1_bit_right_shifter_30_out_3));
  _1_BIT_RIGHT_SHIFTER u_1_bit_right_shifter_31 (
    .C_in__1(Cin__1), .in_2(n1_bit_right_shifter_30_out_3), .out_3(n1_bit_right_shifter_31_out_3));
  Multiplexer #(.select(5), .width(32), .enable("false")) multiplexer_1 (
    .in0(in_2), .in1(n1_bit_right_shifter_1_out_3), .in2(n1_bit_right_shifter_2_out_3),
    .in3(n1_bit_right_shifter_3_out_3), .in4(n1_bit_right_shifter_4_out_3),
    .in5(n1_bit_right_shifter_5_out_3), .in6(n1_bit_right_shifter_6_out_3),
    .in7(n1_bit_right_shifter_7_out_3), .in8(n1_bit_right_shifter_8_out_3),
    .in9(n1_bit_right_shifter_9_out_3), .in10(n1_bit_right_shifter_10_out_3),
    .in11(n1_bit_right_shifter_11_out_3), .in12(n1_bit_right_shifter_12_out_3),
    .in13(n1_bit_right_shifter_13_out_3), .in14(n1_bit_right_shifter_14_out_3),
    .in15(n1_bit_right_shifter_15_out_3), .in16(n1_bit_right_shifter_16_out_3),
    .in17(n1_bit_right_shifter_17_out_3), .in18(n1_bit_right_shifter_18_out_3),
    .in19(n1_bit_right_shifter_19_out_3), .in20(n1_bit_right_shifter_20_out_3),
    .in21(n1_bit_right_shifter_21_out_3), .in22(n1_bit_right_shifter_22_out_3),
    .in23(n1_bit_right_shifter_23_out_3), .in24(n1_bit_right_shifter_24_out_3),
    .in25(n1_bit_right_shifter_25_out_3), .in26(n1_bit_right_shifter_26_out_3),
    .in27(n1_bit_right_shifter_27_out_3), .in28(n1_bit_right_shifter_28_out_3),
    .in29(n1_bit_right_shifter_29_out_3), .in30(n1_bit_right_shifter_30_out_3),
    .in31(n1_bit_right_shifter_31_out_3), .out(out_4), .sel(SA__5));
endmodule

module _1_BIT_RIGHT_SHIFTER (
  input  C_in__1,
  input  [31:0] in_2,
  output [31:0] out_3
);


  assign out_3 = {C_in__1, in_2[31:1]};
endmodule

module _32_BIT_SHIFTER (
  input  [31:0] Input__32,
  input  [4:0] Sa__5,
  input  Cin,
  input  Direction__1,
  output [31:0] out_5
);

  wire [31:0] n32_bit_left_shifter_1_out_4, n32_bit_right_shifter_1_out_4;

  _32_BIT_LEFT_SHIFTER u_32_bit_left_shifter_1 (
    .Cin__1(Cin), .in_2(Input__32), .SA__5(Sa__5), .out_4(n32_bit_left_shifter_1_out_4));
  _32_BIT_RIGHT_SHIFTER u_32_bit_right_shifter_1 (
    .Cin__1(Cin), .in_2(Input__32), .SA__5(Sa__5), .out_4(n32_bit_right_shifter_1_out_4));
  Multiplexer #(.width(32), .enable("false")) multiplexer_1 (
    .in0(n32_bit_left_shifter_1_out_4), .in1(n32_bit_right_shifter_1_out_4), .out(out_5), .sel(Direction__1));
endmodule
