// Logisim project Subtract32.circ as structural Verilog: 5 circuits, main circuit main
module main (
  input  [31:0] in_1,
  input  [31:0] in_2,
  output [31:0] out_3,
  output Carry_out
);

  wire sixteen_bit_subtractor_1_c_out;

  Sixteen_Bit_Subtractor sixteen_bit_subtractor_1 (
    .in_1(in_1[15:0]), .in_2(in_2[15:0]), .C_in(1'b1), .out_4(out_3[15:0]),
    .C_out(sixteen_bit_subtractor_1_c_out));
  Sixteen_Bit_Subtractor sixteen_bit_subtractor_2 (
    .in_1(in_1[31:16]), .in_2(in_2[31:16]), .C_in(sixteen_bit_subtractor_1_c_out), .out_4(out_3[31:16]),
    .C_out(Carry_out));

  // Notes on the sheet:
  //   A in  (32)
  //   B in (32)
  //   Carry in
  //   Out (32)
endmodule

module One_Bit_Subtractor (
  input  A,
  input  B,
  input  C_in,
  output S,
  output out_5
);

  wire and_1_out, and_2_out, not_1_out, or_1_out, xor_1_out;

  not not_1 (not_1_out, B);
  xor xor_1 (xor_1_out, A, not_1_out);
  xor xor_2 (S, xor_1_out, C_in);
  and and_1 (and_1_out, xor_1_out, C_in);
  and and_2 (and_2_out, A, B);
  or or_1 (or_1_out, and_1_out, and_2_out);
  xor xor_3 (out_5, C_in, or_1_out);

  // Notes on the sheet:
  //   C out
endmodule

module Four_Bit_Subtractor (
  input  [3:0] A__4,
  input  [3:0] B__4,
  input  C_in,
  output [3:0] Out,
  output C_out
);

  wire one_bit_subtractor_1_out_5, one_bit_subtractor_2_out_5, one_bit_subtractor_3_out_5;

  One_Bit_Subtractor one_bit_subtractor_1 (
    .A(A__4[0]), .B(B__4[0]), .C_in(C_in), .S(Out[0]), .out_5(one_bit_subtractor_1_out_5));
  One_Bit_Subtractor one_bit_subtractor_2 (
    .A(A__4[1]), .B(B__4[1]), .C_in(one_bit_subtractor_1_out_5), .S(Out[1]),
    .out_5(one_bit_subtractor_2_out_5));
  One_Bit_Subtractor one_bit_subtractor_3 (
    .A(A__4[2]), .B(B__4[2]), .C_in(one_bit_subtractor_2_out_5), .S(Out[2]),
    .out_5(one_bit_subtractor_3_out_5));
  One_Bit_Subtractor one_bit_subtractor_4 (
    .A(A__4[3]), .B(B__4[3]), .C_in(one_bit_subtractor_3_out_5), .S(Out[3]), .out_5(C_out));
endmodule

module Eight_Bit_Subtractor (
  input  [7:0] in_1,
  input  C_in,
  input  [7:0] in_3,
  output [7:0] Out,
  output C_out
);

  wire four_bit_subtractor_1_c_out;

  Four_Bit_Subtractor four_bit_subtractor_1 (
    .A__4(in_1[3:0]), .B__4(in_3[3:0]), .C_in(C_in), .Out(Out[3:0]), .C_out(four_bit_subtractor_1_c_out));
  Four_Bit_Subtractor four_bit_subtractor_2 (
    .A__4(in_1[7:4]), .B__4(in_3[7:4]), .C_in(four_bit_subtractor_1_c_out), .Out(Out[7:4]), .C_out(C_out));

  // Notes on the sheet:
  //   A (8)
  //   B (8)
endmodule

module Sixteen_Bit_Subtractor (
  input  [15:0] in_1,
  input  [15:0] in_2,
  input  C_in,
  output [15:0] out_4,
  output C_out
);

  wire eight_bit_subtractor_1_c_out;

  Eight_Bit_Subtractor eight_bit_subtractor_1 (
    .in_1(in_1[7:0]), .C_in(C_in), .in_3(in_2[7:0]), .Out(out_4[7:0]), .C_out(eight_bit_subtractor_1_c_out));
  Eight_Bit_Subtractor eight_bit_subtractor_2 (
    .in_1(in_1[15:8]), .C_in(eight_bit_subtractor_1_c_out), .in_3(in_2[15:8]), .Out(out_4[15:8]),
    .C_out(C_out));

  // Notes on the sheet:
  //   A in (16)
  //   B in (16)
  //   Out (16)
endmodule
