// Logisim project WRITEBACK MODULE.circ as structural Verilog: 1 circuit, main circuit main
module main (
  input  [31:0] D,
  input  Loadd_Store,
  input  [31:0] M,
  input  Clock,
  output [31:0] result
);

  Multiplexer #(.width(32), .enable("false")) multiplexer_1 (.in0(D), .in1(M), .out(result), .sel(Loadd_Store));
endmodule
